# Fritzing sketch Untitled Sketch arduino montage (saved by Fritzing 0.9.3b)
breadboards: 1

parts:
  Composant1 = Arduino Uno (Rev3)
  Thermi = Temperature Sensor (Thermistor) [thermistor_type=PTC package=THT]
  R3 = Resistor [tolerance=±5% resistance=10k package="2512 [SMD]"]
  Frigo = Peltier Element
  MOSFET = Basic FET N-Channel [package="TO220 [THT]"]
  R4 = Resistor [tolerance=±5% resistance=10k package="0603 [SMD]"]
  DHT22 = Humidity and Temperature Sensor RHT03
  R5 = Resistor [tolerance=±5% resistance=220 package="0603 [SMD]"]

nets:
  N1: Composant1.A0, Thermi.pin_0, R4.Pin_1
  N2: Composant1.GND, Thermi.pin_1, R3.Pin_0, MOSFET.source, DHT22.GND_2
  N3: Composant1.D2, DHT22.Data-signal, R5.Pin_0
  N4: Composant1.D5_PWM, R3.Pin_1, MOSFET.gate
  5V: Composant1.5V, Frigo.pin2, R4.Pin_0, DHT22.Vcc, R5.Pin_1
  N5: Frigo.pin1, MOSFET.drain
